// Logisim project 2.circ as structural Verilog
module main (
  input  a,
  input  b,
  input  c,
  output x,
  output y
);

  wire and_1_out, and_2_out, not_1_out, not_2_out;

  not not_1 (not_1_out, b);
  not not_2 (not_2_out, c);
  and and_1 (and_1_out, a, not_1_out);
  and and_2 (and_2_out, a, not_2_out);
  or or_1 (y, and_1_out, and_2_out);

  assign x = a;
endmodule

module _2 (
  input  a,
  input  b,
  input  c,
  input  d,
  input  e,
  input  f,
  input  g,
  output x,
  output y,
  output z
);

  wire and_1_out, and_2_out, and_3_out, and_4_out, and_5_out, and_6_out, and_7_out, and_8_out, and_9_out,
       not_1_out, not_2_out, not_3_out, not_4_out, not_5_out, not_6_out, not_7_out, not_8_out, not_9_out,
       not_10_out, not_11_out, not_12_out, not_13_out, not_14_out, not_15_out, not_16_out, not_17_out,
       not_18_out, not_19_out, not_20_out, not_21_out, not_22_out, not_23_out, not_24_out, not_25_out,
       not_26_out, not_27_out, not_28_out;

  not not_1 (not_1_out, a);
  not not_2 (not_2_out, a);
  not not_3 (not_3_out, b);
  not not_4 (not_4_out, a);
  not not_5 (not_5_out, b);
  not not_6 (not_6_out, c);
  not not_7 (not_7_out, a);
  not not_8 (not_8_out, a);
  not not_9 (not_9_out, b);
  not not_10 (not_10_out, c);
  not not_11 (not_11_out, d);
  not not_12 (not_12_out, a);
  not not_13 (not_13_out, b);
  not not_14 (not_14_out, c);
  not not_15 (not_15_out, d);
  not not_16 (not_16_out, e);
  not not_17 (not_17_out, a);
  not not_18 (not_18_out, b);
  not not_19 (not_19_out, a);
  not not_20 (not_20_out, b);
  not not_21 (not_21_out, c);
  not not_22 (not_22_out, d);
  not not_23 (not_23_out, a);
  not not_24 (not_24_out, b);
  not not_25 (not_25_out, c);
  not not_26 (not_26_out, d);
  not not_27 (not_27_out, e);
  not not_28 (not_28_out, f);
  and and_1 (and_1_out, not_1_out, b);
  and and_2 (and_2_out, not_2_out, not_3_out, c);
  and and_3 (and_3_out, not_4_out, not_5_out, not_6_out, d);
  and and_4 (and_4_out, not_7_out, b);
  and and_5 (and_5_out, not_8_out, not_9_out, not_10_out, not_11_out, e);
  and and_6 (and_6_out, not_12_out, not_13_out, not_14_out, not_15_out, not_16_out, f);
  and and_7 (and_7_out, not_17_out, not_18_out, c);
  and and_8 (and_8_out, not_19_out, not_20_out, not_21_out, not_22_out, e);
  and and_9 (and_9_out, not_23_out, not_24_out, not_25_out, not_26_out, not_27_out, not_28_out, g);
  or or_1 (x, a, and_1_out, and_2_out, and_3_out);
  or or_2 (y, a, and_4_out, and_5_out, and_6_out);
  or or_3 (z, a, and_7_out, and_8_out, and_9_out);

  // Notes on the sheet:
  //   PB20020586 叶子昂
endmodule
