// Logisim project 13.circ as structural Verilog: 4 circuits, main circuit main
module main (
  input  in_1,
  input  in_2,
  input  [1:0] in_3,
  input  [1:0] in_4,
  input  [1:0] in_5,
  input  [1:0] in_6,
  output [1:0] out_7
);

  wire \与_1_out_3 , \与_2_out_3 , \与_3_out_3 , \与_4_out_3 , \与_5_out_3 , \与_6_out_3 , \与_7_out_3 ,
       \与_8_out_3 , \与_9_out_3 , \与_10_out_3 , \与_11_out_3 , \与_12_out_3 , \或_1_out_3 , \或_2_out_3 ,
       \或_3_out_3 , \或_4_out_3 , \非_1_out_2 , \非_2_out_2 ;

  \非  \u_非_1  (.in_1(in_2), .out_2(\非_1_out_2 ));
  \与  \u_与_1  (.in_1(\非_1_out_2 ), .in_2(in_3[0]), .out_3(\与_1_out_3 ));
  \与  \u_与_2  (.in_1(in_2), .in_2(in_4[0]), .out_3(\与_2_out_3 ));
  \与  \u_与_3  (.in_1(\非_1_out_2 ), .in_2(in_3[1]), .out_3(\与_3_out_3 ));
  \与  \u_与_4  (.in_1(in_2), .in_2(in_4[1]), .out_3(\与_4_out_3 ));
  \与  \u_与_5  (.in_1(\非_1_out_2 ), .in_2(in_5[0]), .out_3(\与_5_out_3 ));
  \与  \u_与_6  (.in_1(in_2), .in_2(in_6[0]), .out_3(\与_6_out_3 ));
  \与  \u_与_7  (.in_1(\非_1_out_2 ), .in_2(in_5[1]), .out_3(\与_7_out_3 ));
  \与  \u_与_8  (.in_1(in_2), .in_2(in_6[1]), .out_3(\与_8_out_3 ));
  \或  \u_或_1  (.in_1(\与_1_out_3 ), .in_2(\与_2_out_3 ), .out_3(\或_1_out_3 ));
  \或  \u_或_2  (.in_1(\与_3_out_3 ), .in_2(\与_4_out_3 ), .out_3(\或_2_out_3 ));
  \或  \u_或_3  (.in_1(\与_5_out_3 ), .in_2(\与_6_out_3 ), .out_3(\或_3_out_3 ));
  \或  \u_或_4  (.in_1(\与_7_out_3 ), .in_2(\与_8_out_3 ), .out_3(\或_4_out_3 ));
  \非  \u_非_2  (.in_1(in_1), .out_2(\非_2_out_2 ));
  \与  \u_与_9  (.in_1(\非_2_out_2 ), .in_2(\或_1_out_3 ), .out_3(\与_9_out_3 ));
  \与  \u_与_10  (.in_1(in_1), .in_2(\或_3_out_3 ), .out_3(\与_10_out_3 ));
  \与  \u_与_11  (.in_1(\非_2_out_2 ), .in_2(\或_2_out_3 ), .out_3(\与_11_out_3 ));
  \与  \u_与_12  (.in_1(in_1), .in_2(\或_4_out_3 ), .out_3(\与_12_out_3 ));
  \或  \u_或_5  (.in_1(\与_9_out_3 ), .in_2(\与_10_out_3 ), .out_3(out_7[0]));
  \或  \u_或_6  (.in_1(\与_11_out_3 ), .in_2(\与_12_out_3 ), .out_3(out_7[1]));
endmodule

module \或  (
  input  in_1,
  input  in_2,
  output out_3
);

  wire transistor_3_out;

  Transistor #(.\type ("n")) transistor_1 (.in(1'b1), .out(out_3), .gate(in_1));
  Transistor transistor_2 (.in(transistor_3_out), .out(out_3), .gate(in_2));
  Transistor transistor_3 (.in(1'b0), .out(transistor_3_out), .gate(in_1));
  Transistor #(.\type ("n")) transistor_4 (.in(1'b1), .out(out_3), .gate(in_2));

  // Notes on the sheet:
  //   叶子昂_PB20020586
endmodule

module \与  (
  input  in_1,
  input  in_2,
  output out_3
);

  wire transistor_1_out;

  Transistor #(.\type ("n")) transistor_1 (.in(1'b1), .out(transistor_1_out), .gate(in_1));
  Transistor #(.\type ("n")) transistor_2 (.in(transistor_1_out), .out(out_3), .gate(in_2));
  Transistor transistor_3 (.in(1'b0), .out(out_3), .gate(in_2));
  Transistor transistor_4 (.in(1'b0), .out(out_3), .gate(in_1));
endmodule

module \非  (
  input  in_1,
  output out_2
);

  Transistor transistor_1 (.in(1'b1), .out(out_2), .gate(in_1));
  Transistor #(.\type ("n")) transistor_2 (.in(1'b0), .out(out_2), .gate(in_1));

  // Notes on the sheet:
  //   叶子昂_PB20020586
endmodule
