// Logisim project 门。.circ as structural Verilog
module main (
  input  in_1,
  input  in_2,
  input  in_3,
  input  in_4,
  output out_5,
  output out_6
);

  wire transistor_1_out, transistor_4_out, transistor_5_out, transistor_9_out, transistor_10_out,
       transistor_15_out;

  Transistor transistor_1 (.in(1'b1), .out(transistor_1_out), .gate(in_1));
  Transistor transistor_2 (.in(transistor_1_out), .out(out_5), .gate(in_3));
  Transistor #(.\type ("n")) transistor_3 (.in(transistor_4_out), .out(out_5), .gate(in_1));
  Transistor transistor_4 (.in(1'b0), .out(transistor_4_out), .gate(in_1));
  Transistor #(.\type ("n")) transistor_5 (.in(1'b1), .out(transistor_5_out), .gate(in_1));
  Transistor #(.\type ("n")) transistor_6 (.in(transistor_5_out), .out(out_5), .gate(in_3));
  Transistor #(.\type ("n")) transistor_7 (.in(transistor_4_out), .out(out_5), .gate(in_3));
  Transistor transistor_8 (.in(1'b0), .out(transistor_4_out), .gate(in_3));
  Transistor transistor_9 (.in(1'b1), .out(transistor_9_out), .gate(in_2));
  Transistor #(.\type ("n")) transistor_10 (.in(1'b1), .out(transistor_10_out), .gate(in_2));
  Transistor #(.\type ("n")) transistor_11 (.in(transistor_9_out), .out(out_6), .gate(in_4));
  Transistor transistor_12 (.in(transistor_10_out), .out(out_6), .gate(in_4));
  Transistor transistor_13 (.in(transistor_15_out), .out(out_6), .gate(in_2));
  Transistor #(.\type ("n")) transistor_14 (.in(transistor_15_out), .out(out_6), .gate(in_4));
  Transistor #(.\type ("n")) transistor_15 (.in(1'b0), .out(transistor_15_out), .gate(in_2));
  Transistor transistor_16 (.in(1'b0), .out(transistor_15_out), .gate(in_4));

  // Notes on the sheet:
  //   叶子昂 PB20020586
  //   叶子昂 PB20020586
endmodule
