// Logisim project eg1.circ as structural Verilog: 18 circuits, main circuit main
module main (
  input  in_1,
  output out_2,
  output out_3
);

  not not_1 (out_2, out_3);
  not not_2 (out_3, out_2);
endmodule

module \S_R锁存器  (
  input  in_1,
  input  in_2,
  output out_3,
  output out_4
);

  wire or_1_out, or_2_out;

  or or_1 (or_1_out, in_1, out_4);
  or or_2 (or_2_out, out_3, in_2);
  not not_1 (out_3, or_1_out);
  not not_2 (out_4, or_2_out);
endmodule

module \D锁存器  (
  input  CLK,
  input  in_2,
  output out_3,
  output out_4
);

  wire and_1_out, and_2_out, not_1_out;

  and and_1 (and_1_out, CLK, not_1_out);
  not not_1 (not_1_out, in_2);
  and and_2 (and_2_out, CLK, in_2);
  \S_R锁存器  \s_r锁存器_1  (.in_1(and_1_out), .in_2(and_2_out), .out_3(out_3), .out_4(out_4));
endmodule

module \D触发器  (
  input  in_1,
  input  D,
  output Q,
  output out_4
);

  wire \d锁存器_1_out_3 , not_1_out;

  not not_1 (not_1_out, in_1);
  \D锁存器  \d锁存器_1  (.in_2(D), .out_3(\d锁存器_1_out_3 ), .CLK(not_1_out));  // open: out_4
  \D锁存器  \d锁存器_2  (.in_2(\d锁存器_1_out_3 ), .out_3(Q), .out_4(out_4), .CLK(in_1));
endmodule

module \同步复位  (
  input  D,
  input  reset,
  output Q,
  output out_4
);

  wire and_1_out, clock_1_out, \d锁存器_1_out_3 , not_1_out, not_2_out;

  Clock clock_1 (.out(clock_1_out));
  not not_1 (not_1_out, clock_1_out);
  and and_1 (and_1_out, D, not_2_out);
  not not_2 (not_2_out, reset);
  \D锁存器  \d锁存器_1  (.in_2(and_1_out), .out_3(\d锁存器_1_out_3 ), .CLK(not_1_out));  // open: out_4
  \D锁存器  \d锁存器_2  (.in_2(\d锁存器_1_out_3 ), .out_3(Q), .out_4(out_4), .CLK(clock_1_out));
endmodule

module \异步复位  (
  input  clk,
  input  D,
  input  reset,
  output Q,
  output out_5
);

  wire not_1_out, or_1_out, \restd锁_1_out_4 ;

  not not_1 (not_1_out, clk);
  \restD锁  \restd锁_1  (.in_1(reset), .CLK(not_1_out), .in_3(D), .out_4(\restd锁_1_out_4 ));  // open: out_5
  or or_1 (or_1_out, clk, reset);
  \D锁存器  \d锁存器_1  (.in_2(\restd锁_1_out_4 ), .out_3(Q), .out_4(out_5), .CLK(or_1_out));
endmodule

module \搭建寄存器  (
  input  in_1,
  input  reset,
  input  [3:0] in_3,
  output [3:0] out_4
);

  wire and_1_out, and_2_out, and_3_out, and_4_out;

  and and_1 (and_1_out, reset, in_3[0]);
  and and_2 (and_2_out, reset, in_3[1]);
  and and_3 (and_3_out, reset, in_3[2]);
  and and_4 (and_4_out, reset, in_3[3]);
  \D触发器  \d触发器_1  (.D(and_1_out), .Q(out_4[0]), .in_1(in_1));  // open: out_4
  \D触发器  \d触发器_2  (.D(and_2_out), .Q(out_4[1]), .in_1(in_1));  // open: out_4
  \D触发器  \d触发器_3  (.D(and_3_out), .Q(out_4[2]), .in_1(in_1));  // open: out_4
  \D触发器  \d触发器_4  (.D(and_4_out), .Q(out_4[3]), .in_1(in_1));  // open: out_4
endmodule

module \搭建时序电路  (
  input  in_1,
  input  [3:0] in_2,
  input  in_3,
  input  [3:0] in_4,
  output [3:0] out_5
);

  wire clock_1_out;
  wire [3:0] adder_1_out;

  Clock clock_1 (.out(clock_1_out));
  Adder #(.width(4)) adder_1 (.a(out_5), .b(in_2), .out(adder_1_out), .cin(in_1));  // open: cout
  \搭建寄存器  \u_搭建寄存器_1  (.in_1(clock_1_out), .reset(in_3), .in_3(adder_1_out), .out_4(out_5));
endmodule

module pr2 (
  input  D,
  input  ret,
  input  re_n,
  output Q,
  output out_5
);

  wire clock_1_out, \d锁存器_1_out_3 , not_1_out, \二选一_1_out_4 , \二选一_2_out_4 ;

  Clock clock_1 (.out(clock_1_out));
  not not_1 (not_1_out, clock_1_out);
  \二选一  \u_二选一_1  (.in_1(re_n), .in_2(D), .in_3(\二选一_2_out_4 ), .out_4(\二选一_1_out_4 ));
  \二选一  \u_二选一_2  (.in_1(ret), .in_2(1'b0), .in_3(1'b1), .out_4(\二选一_2_out_4 ));
  \D锁存器  \d锁存器_1  (.in_2(\二选一_1_out_4 ), .out_3(\d锁存器_1_out_3 ), .CLK(not_1_out));  // open: out_4
  \D锁存器  \d锁存器_2  (.in_2(\d锁存器_1_out_3 ), .out_3(Q), .out_4(out_5), .CLK(clock_1_out));
endmodule

module \二选一  (
  input  in_1,
  input  in_2,
  input  in_3,
  output out_4
);

  wire and_1_out, and_2_out, not_1_out;

  not not_1 (not_1_out, in_1);
  and and_1 (and_1_out, not_1_out, in_2);
  and and_2 (and_2_out, in_1, in_3);
  or or_1 (out_4, and_1_out, and_2_out);
endmodule

module pr3 (
  input  in_1,
  input  in_2,
  output Q0,
  output Q1,
  output Q2,
  output out_6
);

  wire and_1_out, and_2_out, and_3_out, and_4_out, clock_1_out, d_ff_1_q, d_ff_2_q, d_ff_3_q, d_ff_4_q,
       not_1_out, not_2_out, not_3_out, or_1_out, or_2_out, or_3_out, or_4_out, or_5_out, xor_1_out,
       xor_2_out, xor_3_out, xor_4_out;

  Clock clock_1 (.out(clock_1_out));
  not not_1 (not_1_out, in_2);
  D_Flip_Flop d_ff_1 (.clk(clock_1_out), .D(in_2), .Q(d_ff_1_q));  // open: Qn, preset, en, reset
  D_Flip_Flop d_ff_2 (.clk(clock_1_out), .D(not_1_out), .Q(d_ff_2_q));  // open: Qn, preset, en, reset
  D_Flip_Flop d_ff_3 (.clk(clock_1_out), .D(d_ff_1_q), .Q(d_ff_3_q));  // open: Qn, preset, en, reset
  D_Flip_Flop d_ff_4 (.clk(clock_1_out), .D(d_ff_2_q), .Q(d_ff_4_q));  // open: Qn, preset, en, reset
  not not_2 (not_2_out, d_ff_3_q);
  and and_1 (and_1_out, not_2_out, d_ff_1_q);
  not not_3 (not_3_out, d_ff_4_q);
  and and_2 (and_2_out, not_3_out, d_ff_2_q);
  or or_1 (or_1_out, and_1_out, and_2_out);
  xor xor_1 (xor_1_out, 1'b1, Q0);
  or or_2 (or_2_out, in_1, or_1_out);
  // restD锁 restd锁_1: pin names not known; wires that end beside it: xor_1_out, or_2_out, clock_1_out, in_1, Q0
  xor xor_2 (xor_2_out, Q0, Q1);
  or or_3 (or_3_out, in_1, or_1_out);
  // restD锁 restd锁_2: pin names not known; wires that end beside it: xor_2_out, or_3_out, clock_1_out, in_1, Q1
  and and_3 (and_3_out, Q0, Q1);
  xor xor_3 (xor_3_out, and_3_out, Q2);
  or or_4 (or_4_out, in_1, or_1_out);
  // restD锁 restd锁_3: pin names not known; wires that end beside it: xor_3_out, or_4_out, clock_1_out, in_1, Q2
  and and_4 (and_4_out, and_3_out, Q2);
  xor xor_4 (xor_4_out, and_4_out, out_6);
  or or_5 (or_5_out, in_1, or_1_out);
  // restD锁 restd锁_4: pin names not known; wires that end beside it: xor_4_out, or_5_out, clock_1_out, in_1, out_6
endmodule

module pr4 (
  input  rst,
  output Q0,
  output Q1,
  output Q2,
  output Q3
);

  wire and_1_out, and_2_out, clock_1_out, FF0_out_5, FF1_out_5, multiplexer_1_out, multiplexer_2_out,
       not_1_out, \t触发器_1_out_5 , \置位判断_out ;

  Clock clock_1 (.out(clock_1_out));
  not not_1 (not_1_out, clock_1_out);
  nor \u_置位判断  (\置位判断_out , Q0, Q1, Q2, Q3);
  \T触发器  FF0 (.in_3(not_1_out), .in_2(1'b1), .out_4(Q0), .out_5(FF0_out_5), .in_1(rst));
  Multiplexer #(.enable("false")) multiplexer_1 (
    .in0(FF0_out_5), .in1(1'b0), .out(multiplexer_1_out), .sel(\置位判断_out ));
  and and_1 (and_1_out, FF0_out_5, FF1_out_5);
  Multiplexer #(.enable("false")) multiplexer_2 (
    .in0(and_1_out), .in1(1'b0), .out(multiplexer_2_out), .sel(\置位判断_out ));
  \T触发器  FF1 (.in_3(not_1_out), .in_2(multiplexer_1_out), .out_4(Q1), .out_5(FF1_out_5), .in_1(rst));
  \T触发器  \t触发器_1  (.in_3(not_1_out), .in_2(multiplexer_2_out), .out_4(Q2), .out_5(\t触发器_1_out_5 ), .in_1(rst));
  and and_2 (and_2_out, and_1_out, \t触发器_1_out_5 );
  \T触发器  \t触发器_2  (.in_3(not_1_out), .in_2(and_2_out), .out_4(Q3), .in_1(rst));  // open: out_5

  // Notes on the sheet:
  //   FF2
  //   FF3
endmodule

module pr5 (
  input  D,
  input  reset,
  output Q,
  output out_4
);

  wire clock_1_out, \d锁存器_1_out_3 , not_1_out, not_2_out, or_1_out;

  Clock clock_1 (.out(clock_1_out));
  not not_1 (not_1_out, clock_1_out);
  or or_1 (or_1_out, ~D, reset);  // OR_Gate
  \D锁存器  \d锁存器_1  (.in_2(not_2_out), .out_3(\d锁存器_1_out_3 ), .CLK(not_1_out));  // open: out_4
  not not_2 (not_2_out, or_1_out);
  \D锁存器  \d锁存器_2  (.in_2(\d锁存器_1_out_3 ), .out_3(Q), .out_4(out_4), .CLK(clock_1_out));
endmodule

module pr6 (
  input  reset,
  output Q0,
  output Q1,
  output Q2,
  output Q3
);

  wire and_1_out, and_2_out, clock_1_out, xor_1_out, xor_2_out, xor_3_out, xor_4_out;

  Clock clock_1 (.out(clock_1_out));
  xor xor_1 (xor_1_out, 1'b1, Q0);
  \异步复位  \u_异步复位_1  (.D(xor_1_out), .reset(reset), .Q(Q0), .clk(clock_1_out));  // open: out_5
  xor xor_2 (xor_2_out, Q0, Q1);
  and and_1 (and_1_out, Q0, Q1);
  \异步复位  \u_异步复位_2  (.D(xor_2_out), .reset(reset), .Q(Q1), .clk(clock_1_out));  // open: out_5
  xor xor_3 (xor_3_out, and_1_out, Q2);
  and and_2 (and_2_out, and_1_out, Q2);
  \异步复位  \u_异步复位_3  (.D(xor_3_out), .reset(reset), .Q(Q2), .clk(clock_1_out));  // open: out_5
  xor xor_4 (xor_4_out, and_2_out, Q3);
  \异步复位  \u_异步复位_4  (.D(xor_4_out), .reset(reset), .Q(Q3), .clk(clock_1_out));  // open: out_5
endmodule

module \restD锁  (
  input  in_1,
  input  CLK,
  input  in_3,
  output out_4,
  output out_5
);

  wire and_1_out, and_2_out, not_1_out, or_1_out;

  and and_1 (and_1_out, CLK, not_1_out);
  not not_1 (not_1_out, in_3);
  and and_2 (and_2_out, CLK, in_3);
  or or_1 (or_1_out, in_1, and_1_out);
  \S_R锁存器  \s_r锁存器_1  (.in_1(or_1_out), .in_2(and_2_out), .out_3(out_4), .out_4(out_5));
endmodule

module \T触发器  (
  input  in_1,
  input  in_2,
  input  in_3,
  output out_4,
  output out_5
);

  wire xor_1_out;

  xor xor_1 (xor_1_out, out_4, in_2);
  \异步复位  \u_异步复位_1  (.D(xor_1_out), .reset(in_1), .Q(out_4), .out_5(out_5), .clk(in_3));
endmodule

module pr83 (
  input  sw,
  input  rst,
  output Q0,
  output Q1,
  output Q2,
  output out_6,
  output [3:0] cnt
);

  wire and_1_out, and_2_out, and_3_out, and_4_out, clock_1_out, d_ff_1_q, d_ff_2_q, d_ff_3_q, d_ff_4_q,
       multiplexer_1_out, multiplexer_2_out, multiplexer_3_out, multiplexer_4_out, not_1_out, not_2_out,
       not_3_out, or_1_out, xor_1_out, xor_2_out, xor_3_out, xor_4_out;

  Clock clock_1 (.out(clock_1_out));
  D_Flip_Flop d_ff_1 (.clk(clock_1_out), .D(sw), .Q(d_ff_1_q));  // open: Qn, preset, en, reset
  D_Flip_Flop d_ff_2 (.clk(clock_1_out), .D(not_1_out), .Q(d_ff_2_q));  // open: Qn, preset, en, reset
  not not_1 (not_1_out, sw);
  D_Flip_Flop d_ff_3 (.clk(clock_1_out), .D(d_ff_1_q), .Q(d_ff_3_q));  // open: Qn, preset, en, reset
  D_Flip_Flop d_ff_4 (.clk(clock_1_out), .D(d_ff_2_q), .Q(d_ff_4_q));  // open: Qn, preset, en, reset
  not not_2 (not_2_out, d_ff_3_q);
  not not_3 (not_3_out, d_ff_4_q);
  and and_1 (and_1_out, not_2_out, d_ff_1_q);
  and and_2 (and_2_out, not_3_out, d_ff_2_q);
  xor xor_1 (xor_1_out, 1'b1, cnt[3]);
  Multiplexer #(.enable("false")) multiplexer_1 (
    .in0(cnt[3]), .in1(xor_1_out), .out(multiplexer_1_out), .sel(or_1_out));
  or or_1 (or_1_out, and_1_out, and_2_out);
  \异步复位  \u_异步复位_1  (.D(multiplexer_1_out), .reset(rst), .Q(cnt[3]), .clk(clock_1_out));  // open: out_5
  xor xor_2 (xor_2_out, cnt[3], cnt[2]);
  Multiplexer #(.enable("false")) multiplexer_2 (
    .in0(cnt[2]), .in1(xor_2_out), .out(multiplexer_2_out), .sel(or_1_out));
  \异步复位  \u_异步复位_2  (.D(multiplexer_2_out), .reset(rst), .Q(cnt[2]), .clk(clock_1_out));  // open: out_5
  and and_3 (and_3_out, cnt[3], cnt[2]);
  xor xor_3 (xor_3_out, and_3_out, cnt[1]);
  Multiplexer #(.enable("false")) multiplexer_3 (
    .in0(cnt[1]), .in1(xor_3_out), .out(multiplexer_3_out), .sel(or_1_out));
  \异步复位  \u_异步复位_3  (.D(multiplexer_3_out), .reset(rst), .Q(cnt[1]), .clk(clock_1_out));  // open: out_5
  and and_4 (and_4_out, and_3_out, cnt[1]);
  xor xor_4 (xor_4_out, and_4_out, cnt[0]);
  Multiplexer #(.enable("false")) multiplexer_4 (
    .in0(cnt[0]), .in1(xor_4_out), .out(multiplexer_4_out), .sel(or_1_out));
  \异步复位  \u_异步复位_4  (.D(multiplexer_4_out), .reset(rst), .Q(cnt[0]), .clk(clock_1_out));  // open: out_5

  assign out_6 = cnt[0];
  assign Q0 = cnt[3];
  assign Q1 = cnt[2];
  assign Q2 = cnt[1];
endmodule

module pr831 (
  input  in_1,
  input  in_2,
  output Q0,
  output Q1,
  output Q2,
  output out_6
);

  wire and_1_out, and_2_out, and_3_out, and_4_out, clock_1_out, d_ff_1_q, d_ff_2_q, d_ff_3_q, d_ff_4_q,
       not_1_out, not_2_out, not_3_out, or_1_out, or_2_out, or_3_out, or_4_out, or_5_out, xor_1_out,
       xor_2_out, xor_3_out, xor_4_out;

  Clock clock_1 (.out(clock_1_out));
  not not_1 (not_1_out, in_2);
  D_Flip_Flop d_ff_1 (.clk(clock_1_out), .D(in_2), .Q(d_ff_1_q));  // open: Qn, preset, en, reset
  D_Flip_Flop d_ff_2 (.clk(clock_1_out), .D(not_1_out), .Q(d_ff_2_q));  // open: Qn, preset, en, reset
  D_Flip_Flop d_ff_3 (.clk(clock_1_out), .D(d_ff_1_q), .Q(d_ff_3_q));  // open: Qn, preset, en, reset
  D_Flip_Flop d_ff_4 (.clk(clock_1_out), .D(d_ff_2_q), .Q(d_ff_4_q));  // open: Qn, preset, en, reset
  not not_2 (not_2_out, d_ff_3_q);
  and and_1 (and_1_out, not_2_out, d_ff_1_q);
  not not_3 (not_3_out, d_ff_4_q);
  and and_2 (and_2_out, not_3_out, d_ff_2_q);
  or or_1 (or_1_out, and_1_out, and_2_out);
  xor xor_1 (xor_1_out, 1'b1, Q0);
  or or_2 (or_2_out, in_1, or_1_out);
  // restD锁 restd锁_1: pin names not known; wires that end beside it: xor_1_out, or_2_out, clock_1_out, in_1, Q0
  xor xor_2 (xor_2_out, Q0, Q1);
  or or_3 (or_3_out, in_1, or_1_out);
  // restD锁 restd锁_2: pin names not known; wires that end beside it: xor_2_out, or_3_out, clock_1_out, in_1, Q1
  and and_3 (and_3_out, Q0, Q1);
  xor xor_3 (xor_3_out, and_3_out, Q2);
  or or_4 (or_4_out, in_1, or_1_out);
  // restD锁 restd锁_3: pin names not known; wires that end beside it: xor_3_out, or_4_out, clock_1_out, in_1, Q2
  and and_4 (and_4_out, and_3_out, Q2);
  xor xor_4 (xor_4_out, and_4_out, out_6);
  or or_5 (or_5_out, in_1, or_1_out);
  // restD锁 restd锁_4: pin names not known; wires that end beside it: xor_4_out, or_5_out, clock_1_out, in_1, out_6
endmodule
