// Logisim project pr.circ as structural Verilog: 1 circuit, main circuit main
module main (
  input  \S非 ,
  input  \R非 ,
  output out_3,
  output out_4
);

  nand nand_1 (out_3, \S非 , out_4);
  nand nand_2 (out_4, out_3, \R非 );
endmodule
