// Logisim project 名字.circ as structural Verilog: 1 circuit, main circuit main
module main (
  input  [14:0] in_1,
  input  [14:0] in_2,
  input  [14:0] in_3,
  input  [14:0] in_4,
  input  [14:0] in_5,
  input  [14:0] in_6,
  input  [14:0] in_7,
  input  [14:0] in_8,
  input  [14:0] in_9,
  input  [14:0] in_10,
  input  [14:0] in_11,
  input  [14:0] in_12,
  input  [14:0] in_13,
  input  [14:0] in_14,
  input  [14:0] in_15,
  input  [14:0] in_16,
  input  [14:0] in_17,
  input  [14:0] in_18,
  input  [14:0] in_19,
  input  [14:0] in_20,
  input  [14:0] in_21,
  input  [14:0] in_22,
  input  [14:0] in_23,
  input  [14:0] in_24,
  input  [14:0] in_25,
  input  [14:0] in_26,
  input  [14:0] in_27,
  input  [14:0] in_28,
  input  [14:0] in_29,
  input  [14:0] in_30,
  input  [14:0] in_31,
  input  [14:0] in_32
);

  DotMatrix #(.matrixcols(32), .matrixrows(15), .dotshape("circle")) dotmatrix_1 (
    .col0(in_1), .col1(in_5), .col2(in_9), .col3(in_13), .col4(in_17), .col5(in_3), .col6(in_7),
    .col7(in_11), .col8(in_15), .col9(in_19), .col10(in_21), .col11(in_23), .col12(in_25), .col13(in_27),
    .col14(in_29), .col15(in_31), .col16(in_32), .col17(in_30), .col18(in_28), .col19(in_26), .col20(in_24),
    .col21(in_22), .col22(in_20), .col23(in_16), .col24(in_12), .col25(in_8), .col26(in_4), .col27(in_18),
    .col28(in_14), .col29(in_10), .col30(in_6), .col31(in_2));
endmodule
