// Logisim project 门.circ as structural Verilog: 7 circuits, main circuit main
module main (
  input  in_1,
  input  in_2,
  input  in_3,
  input  in_4,
  input  in_5,
  input  in_6,
  input  in_7,
  input  in_8,
  input  in_9,
  input  [1:0] in_10,
  output out_11,
  output out_12
);

  wire \与_1_out_3 , \与_2_out_3 , \与_3_out_3 , \与_4_out_3 , \与_5_out_3 , \与_6_out_3 , \与_7_out_3 ,
       \与_8_out_3 , \或_2_out_3 , \或_3_out_3 , \非_1_out_2 , \非_2_out_2 , \非_3_out_2 , \非_4_out_2 ;

  \非  \u_非_1  (.in_1(in_1), .out_2(\非_1_out_2 ));
  \非  \u_非_2  (.in_1(in_5), .out_2(\非_2_out_2 ));
  \非  \u_非_3  (.in_1(in_5), .out_2(\非_3_out_2 ));
  \与  \u_与_1  (.in_1(in_2), .in_2(\非_1_out_2 ), .out_3(\与_1_out_3 ));
  \与  \u_与_2  (.in_1(in_3), .in_2(in_1), .out_3(\与_2_out_3 ));
  \与  \u_与_3  (.in_1(in_6), .in_2(\非_2_out_2 ), .out_3(\与_3_out_3 ));
  \与  \u_与_4  (.in_1(in_7), .in_2(in_5), .out_3(\与_4_out_3 ));
  \与  \u_与_5  (.in_1(in_8), .in_2(\非_3_out_2 ), .out_3(\与_5_out_3 ));
  \与  \u_与_6  (.in_1(in_9), .in_2(in_5), .out_3(\与_6_out_3 ));
  \或  \u_或_1  (.in_1(\与_1_out_3 ), .in_2(\与_2_out_3 ), .out_3(out_11));
  \或  \u_或_2  (.in_1(\与_3_out_3 ), .in_2(\与_4_out_3 ), .out_3(\或_2_out_3 ));
  \或  \u_或_3  (.in_1(\与_5_out_3 ), .in_2(\与_6_out_3 ), .out_3(\或_3_out_3 ));
  \非  \u_非_4  (.in_1(in_4), .out_2(\非_4_out_2 ));
  \与  \u_与_7  (.in_1(\或_2_out_3 ), .in_2(\非_4_out_2 ), .out_3(\与_7_out_3 ));
  \与  \u_与_8  (.in_1(\或_3_out_3 ), .in_2(in_4), .out_3(\与_8_out_3 ));
  \或  \u_或_4  (.in_1(\与_7_out_3 ), .in_2(\与_8_out_3 ), .out_3(out_12));
endmodule

module \与  (
  input  in_1,
  input  in_2,
  output out_3
);

  wire transistor_1_out;

  Transistor #(.\type ("n")) transistor_1 (.in(1'b1), .out(transistor_1_out), .gate(in_1));
  Transistor #(.\type ("n")) transistor_2 (.in(transistor_1_out), .out(out_3), .gate(in_2));
  Transistor transistor_3 (.in(1'b0), .out(out_3), .gate(in_2));
  Transistor transistor_4 (.in(1'b0), .out(out_3), .gate(in_1));

  // Notes on the sheet:
  //   叶子昂_PB20020586
endmodule

module \或  (
  input  in_1,
  input  in_2,
  output out_3
);

  wire transistor_3_out;

  Transistor #(.\type ("n")) transistor_1 (.in(1'b1), .out(out_3), .gate(in_1));
  Transistor transistor_2 (.in(transistor_3_out), .out(out_3), .gate(in_2));
  Transistor transistor_3 (.in(1'b0), .out(transistor_3_out), .gate(in_1));
  Transistor #(.\type ("n")) transistor_4 (.in(1'b1), .out(out_3), .gate(in_2));

  // Notes on the sheet:
  //   叶子昂_PB20020586
endmodule

module \非  (
  input  in_1,
  output out_2
);

  Transistor transistor_1 (.in(1'b1), .out(out_2), .gate(in_1));
  Transistor #(.\type ("n")) transistor_2 (.in(1'b0), .out(out_2), .gate(in_1));

  // Notes on the sheet:
  //   叶子昂_PB20020586
endmodule

module \或非  (
  input  in_1,
  input  in_2,
  output out_3
);

  wire transistor_1_out, transistor_3_out;

  Transistor #(.\type ("n")) transistor_1 (.in(1'b1), .out(transistor_1_out), .gate(in_1));
  Transistor transistor_2 (.in(transistor_3_out), .out(transistor_1_out), .gate(in_2));
  Transistor transistor_3 (.in(1'b0), .out(transistor_3_out), .gate(in_1));
  Transistor #(.\type ("n")) transistor_4 (.in(1'b1), .out(transistor_1_out), .gate(in_2));
  Transistor transistor_5 (.in(1'b1), .out(out_3), .gate(transistor_1_out));
  Transistor #(.\type ("n")) transistor_6 (.in(1'b0), .out(out_3), .gate(transistor_1_out));

  // Notes on the sheet:
  //   叶子昂_PB20020586
endmodule

module \与非  (
  input  in_1,
  input  in_2,
  output out_3
);

  wire transistor_1_out, transistor_2_out;

  Transistor transistor_1 (.in(1'b0), .out(transistor_1_out), .gate(in_2));
  Transistor #(.\type ("n")) transistor_2 (.in(1'b1), .out(transistor_2_out), .gate(in_1));
  Transistor #(.\type ("n")) transistor_3 (.in(transistor_2_out), .out(transistor_1_out), .gate(in_2));
  Transistor transistor_4 (.in(1'b0), .out(transistor_1_out), .gate(in_1));
  Transistor transistor_5 (.in(1'b1), .out(out_3), .gate(transistor_1_out));
  Transistor #(.\type ("n")) transistor_6 (.in(1'b0), .out(out_3), .gate(transistor_1_out));

  // Notes on the sheet:
  //   叶子昂_PB20020586
endmodule

module _4 (
  input  in_1,
  input  [1:0] in_2,
  input  [1:0] in_3,
  input  [1:0] in_4,
  input  [1:0] in_5
);

  wire \与_3_out_3 , \与_4_out_3 , \或_1_out_3 , \非_1_out_2 ;

  \非  \u_非_1  (.in_1(in_1), .out_2(\非_1_out_2 ));
  \与  \u_与_1  (.in_1(\非_1_out_2 ));  // open: in_2, out_3
  \与  \u_与_2  ();  // open: in_1, in_2, out_3
  \与  \u_与_3  (.in_1(\非_1_out_2 ), .in_2(in_2[1]), .out_3(\与_3_out_3 ));
  \与  \u_与_4  (.in_1(in_1), .in_2(in_3[1]), .out_3(\与_4_out_3 ));
  \或  \u_或_1  (.in_1(\与_3_out_3 ), .in_2(\与_4_out_3 ), .out_3(\或_1_out_3 ));
endmodule
